// Logisim project eLC-3.circ as structural Verilog: 2 circuits, main circuit eLC-3
module eLC_3 (
);

  wire and_2_out, CLOCK, e0, e1, e2, e3, e4, e5, e6, e7, GateALU, GateMDR, GateOFFSET, GatePC, GateREG,
       LD_CC, LD_IR, LD_MAR, LD_MDR, LD_PC, LD_REG, MEM_EN, MEM_RW, MIO_EN, not_1_out, not_2_out, PCMUX,
       SR2MUX;
  wire [1:0] ALUK;
  wire [2:0] CC_q, comparator_1_gt, IR_2_0, IR_8_6, IR_11_9, SR1;
  wire [3:0] OPCODE;
  wire [4:3] IR_4_0;
  wire [5:5] PCOFF;
  wire [15:0] adder_1_out, adder_2_out, adder_3_out, and_1_out, bit_extender_1_out, bit_extender_2_out,
       controlled_buffer_1_out, MAR_q, MDR_q, multiplexer_1_out, multiplexer_2_out, multiplexer_3_out,
       multiplexer_4_out, multiplexer_5_out, multiplexer_6_out, not_3_out, PC_q, R0, R1, R2, R3, R4, R5, R6,
       R7, ram_1_data;

  assign controlled_buffer_1_out = GateOFFSET ? adder_1_out : 16'bz;  // Controlled_Buffer controlled_buffer_1
  Multiplexer #(.width(16), .enable("false")) multiplexer_1 (
    .in0(adder_1_out), .in1(adder_2_out), .out(multiplexer_1_out), .sel(PCMUX));
  Adder #(.width(16)) adder_1 (.a(bit_extender_1_out), .b(PC_q), .out(adder_1_out), .cin(1'b0));  // open: cout
  assign bit_extender_1_out = {{7{IR_8_6[2]}}, {IR_8_6, PCOFF[5], IR_4_0, IR_2_0}};  // Bit_Extender bit_extender_1
  Register #(.width(16)) IR (
    .D(controlled_buffer_1_out), .en(LD_IR), .Q({OPCODE, IR_11_9, IR_8_6, PCOFF[5], IR_4_0, IR_2_0}),
    .clk(CLOCK));  // open: clr
  Multiplexer #(.width(16), .enable("false")) multiplexer_2 (
    .in0(controlled_buffer_1_out), .in1(ram_1_data), .out(multiplexer_2_out), .sel(MIO_EN));
  assign controlled_buffer_1_out = GatePC ? PC_q : 16'bz;  // Controlled_Buffer controlled_buffer_2
  Register #(.width(16)) PC (.D(multiplexer_1_out), .en(LD_PC), .Q(PC_q), .clk(CLOCK));  // open: clr
  assign controlled_buffer_1_out = GateMDR ? MDR_q : 16'bz;  // Controlled_Buffer controlled_buffer_3
  Register #(.width(16)) MDR (.D(multiplexer_2_out), .en(LD_MDR), .Q(MDR_q), .clk(CLOCK));  // open: clr
  Adder #(.width(16)) adder_2 (.a(PC_q), .b(16'h1), .out(adder_2_out), .cin(1'b0));  // open: cout
  Comparator #(.width(16)) comparator_1 (
    .a(controlled_buffer_1_out), .b({16{1'b0}}), .gt(comparator_1_gt[0]), .eq(comparator_1_gt[1]),
    .lt(comparator_1_gt[2]));
  Clock clock_1 (.out(CLOCK));
  Register #(.width(3)) CC (.D(comparator_1_gt), .en(LD_CC), .Q(CC_q), .clk(CLOCK));  // open: clr
  RAM #(.addrWidth(16), .dataWidth(16), .bus("separate")) ram_1 (
    .addr(MAR_q), .din(MDR_q), .data(ram_1_data), .str(MEM_RW), .sel(MEM_EN), .clk(CLOCK), .ld(not_1_out));  // open: clr
  not not_1 (not_1_out, MEM_RW);
  Demultiplexer #(.select(3), .disabled(0)) demultiplexer_1 (
    .out0(e0), .out1(e1), .out2(e2), .out3(e3), .out4(e4), .out5(e5), .out6(e6), .out7(e7), .in(1'b1),
    .sel(IR_11_9), .en(LD_REG));
  Controller FSM (
    .CLOCK(CLOCK), .IR({OPCODE, IR_11_9, IR_8_6, PCOFF[5], IR_4_0, IR_2_0}), .CC(CC_q), .ALUK(ALUK),
    .GateALU(GateALU), .GateMDR(GateMDR), .GateOFFSET(GateOFFSET), .GatePC(GatePC), .GateREG(GateREG),
    .LD_CC(LD_CC), .LD_IR(LD_IR), .LD_MAR(LD_MAR), .LD_MDR(LD_MDR), .LD_REG(LD_REG), .LD_PC(LD_PC),
    .MEM_EN(MEM_EN), .MEM_RW(MEM_RW), .MIO_EN(MIO_EN), .PCMUX(PCMUX), .SR2MUX(SR2MUX));
  Register #(.width(16)) MAR (.D(controlled_buffer_1_out), .en(LD_MAR), .Q(MAR_q), .clk(CLOCK));  // open: clr
  Register #(.width(16)) u_R0 (.D(controlled_buffer_1_out), .en(e0), .Q(R0), .clk(CLOCK));  // open: clr
  Register #(.width(16)) u_R4 (.D(controlled_buffer_1_out), .en(e4), .Q(R4), .clk(CLOCK));  // open: clr
  Multiplexer #(.select(3), .width(16), .enable("false")) multiplexer_3 (
    .in0(R0), .in1(R1), .in2(R2), .in3(R3), .in4(R4), .in5(R5), .in6(R6), .in7(R7), .out(multiplexer_3_out),
    .sel(IR_2_0));
  assign bit_extender_2_out = {{11{IR_4_0[4]}}, {IR_4_0, IR_2_0}};  // Bit_Extender bit_extender_2
  not not_2 (not_2_out, SR2MUX);
  Multiplexer #(.width(16), .enable("false")) multiplexer_4 (
    .in0(bit_extender_2_out), .in1(multiplexer_3_out), .out(multiplexer_4_out), .sel(not_2_out));
  // Probe on multiplexer_4_out
  Register #(.width(16)) u_R1 (.D(controlled_buffer_1_out), .en(e1), .Q(R1), .clk(CLOCK));  // open: clr
  Register #(.width(16)) u_R5 (.D(controlled_buffer_1_out), .en(e5), .Q(R5), .clk(CLOCK));  // open: clr
  Adder #(.width(16)) adder_3 (
    .a(multiplexer_5_out), .b(multiplexer_4_out), .out(adder_3_out), .cin(1'b0));  // open: cout
  assign and_1_out = multiplexer_5_out & multiplexer_4_out;  // AND_Gate and_1, 16 bits wide
  assign not_3_out = ~multiplexer_5_out;  // NOT_Gate not_3, 16 bits wide
  Register #(.width(16)) u_R2 (.D(controlled_buffer_1_out), .en(e2), .Q(R2), .clk(CLOCK));  // open: clr
  Register #(.width(16)) u_R6 (.D(controlled_buffer_1_out), .en(e6), .Q(R6), .clk(CLOCK));  // open: clr
  Multiplexer #(.select(3), .width(16), .enable("false")) multiplexer_5 (
    .in0(R0), .in1(R1), .in2(R2), .in3(R3), .in4(R4), .in5(R5), .in6(R6), .in7(R7), .out(multiplexer_5_out),
    .sel(SR1));
  // Probe on multiplexer_5_out
  Multiplexer #(.select(2), .width(16), .enable("false")) multiplexer_6 (
    .in0(adder_3_out), .in1(and_1_out), .in2(not_3_out), .out(multiplexer_6_out), .sel(ALUK));  // open: in3
  assign controlled_buffer_1_out = GateALU ? multiplexer_6_out : 16'bz;  // Controlled_Buffer controlled_buffer_4
  Register #(.width(16)) u_R3 (.D(controlled_buffer_1_out), .en(e3), .Q(R3), .clk(CLOCK));  // open: clr
  Register #(.width(16)) u_R7 (.D(controlled_buffer_1_out), .en(e7), .Q(R7), .clk(CLOCK));  // open: clr
  assign controlled_buffer_1_out = GateREG ? multiplexer_5_out : 16'bz;  // Controlled_Buffer GateREG
  and and_2 (and_2_out, OPCODE[0], OPCODE[1], ~OPCODE[2], ~OPCODE[3]);  // AND_Gate
  // Probe on controlled_buffer_1_out
  Multiplexer #(.width(3), .enable("false")) multiplexer_7 (.in0(IR_8_6), .in1(IR_11_9), .out(SR1), .sel(and_2_out));

  // Other names for the same wires on the sheet: IR_4_0[2:0] = IR_2_0; PCOFF (some bits) = {IR_8_6, IR_4_0, IR_2_0}

  // Notes on the sheet:
  //   eLC-3 DATAPATH
  //   INPUT SECTION: Do not change anything here!
  //   To test, load a file into memory and tick the clock.
  //   MEMORY
  //   REG FILE
  //   ALU
  //   LOGIC FOR SR1
endmodule

module Controller (
  input  CLOCK,
  input  [15:0] IR,
  input  [2:0] CC,
  output [1:0] ALUK,
  output GateALU,
  output GateMDR,
  output GateOFFSET,
  output GatePC,
  output GateREG,
  output LD_CC,
  output LD_IR,
  output LD_MAR,
  output LD_MDR,
  output LD_REG,
  output LD_PC,
  output MEM_EN,
  output MEM_RW,
  output MIO_EN,
  output PCMUX,
  output SR2MUX
);

  wire _1, _2, _3, _4, _5, _6, _7, _8, _9, _10, _11, _12, _13, _14, _15, _16, and_1_out, and_2_out,
       and_3_out, not_1_out, not_2_out, not_3_out, not_4_out, not_5_out, not_6_out, not_7_out, not_8_out,
       not_9_out, not_10_out, not_11_out, not_12_out, not_13_out, not_14_out, not_15_out, not_16_out,
       not_17_out, not_18_out, not_19_out, not_20_out, not_21_out, not_22_out, not_23_out, not_24_out,
       not_25_out, not_26_out, not_27_out, not_28_out, not_29_out, not_30_out, not_31_out, not_32_out,
       not_33_out, not_34_out, not_35_out, not_36_out, not_37_out, not_38_out, not_39_out, not_40_out,
       not_41_out, not_42_out, not_43_out, not_44_out, not_45_out, not_46_out, not_47_out, not_48_out,
       not_49_out, not_50_out, not_51_out, not_52_out, not_53_out, not_54_out, not_55_out, not_56_out,
       not_57_out, not_58_out, not_59_out, not_60_out, or_1_out, S0, S0n_out, S1, S1n_out, S2, S2n_out;

  and and_1 (and_1_out, CC[2], IR[11]);
  and and_2 (and_2_out, CC[1], IR[10]);
  or or_1 (or_1_out, and_1_out, and_2_out, and_3_out);
  and and_3 (and_3_out, CC[0], IR[9]);
  not not_1 (not_1_out, S2);
  not not_2 (not_2_out, S1);
  not not_3 (not_3_out, S0);
  not not_4 (not_4_out, S2);
  not not_5 (not_5_out, S1);
  not not_6 (not_6_out, S2);
  not not_7 (not_7_out, S0);
  not not_8 (not_8_out, IR[14]);
  not not_9 (not_9_out, IR[13]);
  not not_10 (not_10_out, S2);
  not not_11 (not_11_out, IR[15]);
  not not_12 (not_12_out, IR[14]);
  not not_13 (not_13_out, IR[13]);
  not not_14 (not_14_out, S2);
  not not_15 (not_15_out, IR[5]);
  not not_16 (not_16_out, IR[15]);
  not not_17 (not_17_out, IR[14]);
  not not_18 (not_18_out, IR[13]);
  not not_19 (not_19_out, S2);
  not not_20 (not_20_out, IR[15]);
  not not_21 (not_21_out, IR[13]);
  not not_22 (not_22_out, S2);
  not not_23 (not_23_out, IR[5]);
  not not_24 (not_24_out, IR[15]);
  not not_25 (not_25_out, IR[13]);
  not not_26 (not_26_out, S2);
  not not_27 (not_27_out, IR[15]);
  not not_28 (not_28_out, IR[14]);
  not not_29 (not_29_out, IR[12]);
  not not_30 (not_30_out, S2);
  not not_31 (not_31_out, IR[15]);
  not not_32 (not_32_out, IR[14]);
  not not_33 (not_33_out, IR[12]);
  not not_34 (not_34_out, S1);
  not not_35 (not_35_out, S0);
  not not_36 (not_36_out, IR[15]);
  not not_37 (not_37_out, IR[14]);
  not not_38 (not_38_out, IR[12]);
  not not_39 (not_39_out, S1);
  not not_40 (not_40_out, IR[15]);
  not not_41 (not_41_out, IR[14]);
  not not_42 (not_42_out, IR[13]);
  not not_43 (not_43_out, IR[12]);
  not not_44 (not_44_out, S2);
  not not_45 (not_45_out, IR[15]);
  not not_46 (not_46_out, IR[14]);
  not not_47 (not_47_out, IR[13]);
  not not_48 (not_48_out, IR[12]);
  not not_49 (not_49_out, S2);
  not not_50 (not_50_out, or_1_out);
  not not_51 (not_51_out, IR[15]);
  not not_52 (not_52_out, IR[14]);
  not not_53 (not_53_out, S2);
  not not_54 (not_54_out, IR[15]);
  not not_55 (not_55_out, IR[14]);
  not not_56 (not_56_out, S1);
  not not_57 (not_57_out, S0);
  not not_58 (not_58_out, IR[15]);
  not not_59 (not_59_out, IR[14]);
  not not_60 (not_60_out, S1);
  and Fetch_1 (_1, not_1_out, not_2_out, not_3_out);
  and Fetch_2 (_2, not_4_out, not_5_out, S0);
  and Fetch_3 (_3, not_6_out, S1, not_7_out);
  and NOT_4_dup2 (_4, IR[15], not_8_out, not_9_out, IR[12], not_10_out, S1, S0);
  and ADDS_4 (_5, not_11_out, not_12_out, not_13_out, IR[12], not_14_out, S1, S0, not_15_out);
  and ADDI_4 (_6, not_16_out, not_17_out, not_18_out, IR[12], not_19_out, S1, S0, IR[5]);
  and ANDS_4 (_7, not_20_out, IR[14], not_21_out, IR[12], not_22_out, S1, S0, not_23_out);
  and ANDI_4 (_8, not_24_out, IR[14], not_25_out, IR[12], not_26_out, S1, S0, IR[5]);
  and LD_4 (_9, not_27_out, not_28_out, IR[13], not_29_out, not_30_out, S1, S0);
  and LD_5 (_10, not_31_out, not_32_out, IR[13], not_33_out, S2, not_34_out, not_35_out);
  and LD_6 (_11, not_36_out, not_37_out, IR[13], not_38_out, S2, not_39_out, S0);
  and BRHit_4 (_12, not_40_out, not_41_out, not_42_out, not_43_out, not_44_out, S1, S0, or_1_out);
  and BR_nHit (_13, not_45_out, not_46_out, not_47_out, not_48_out, not_49_out, S1, S0, not_50_out);
  and ST_4 (_14, not_51_out, not_52_out, IR[13], IR[12], not_53_out, S1, S0);
  and ST_5 (_15, not_54_out, not_55_out, IR[13], IR[12], S2, not_56_out, not_57_out);
  and ST_6 (_16, not_58_out, not_59_out, IR[13], IR[12], S2, not_60_out, S0);
  or S2n (S2n_out, _9, _10, _14, _15);
  or or_2 (MIO_EN, _2, _10);
  or or_3 (GateMDR, _3, _11);
  or or_4 (PCMUX, _1, _13);
  buf or_5 (ALUK[1], _4);  // OR_Gate
  or or_6 (LD_CC, _11, _4, _5, _7, _8, _6);
  D_Flip_Flop u_S2 (.clk(CLOCK), .D(S2n_out), .Q(S2));  // open: Qn, preset, en, reset
  D_Flip_Flop u_S1 (.clk(CLOCK), .D(S1n_out), .Q(S1));  // open: Qn, preset, en, reset
  D_Flip_Flop u_S0 (.clk(CLOCK), .D(S0n_out), .Q(S0));  // open: Qn, preset, en, reset
  or S1n (S1n_out, _2, _3);
  buf or_7 (MEM_RW, _16);  // OR_Gate
  or or_8 (LD_MAR, _1, _9, _13, _14);
  or or_9 (LD_PC, _1, _12, _13);
  or or_10 (ALUK[0], _7, _8);
  or or_11 (LD_REG, _6, _4, _5, _7, _8, _11);
  or S0n (S0n_out, _1, _3, _10, _13, _15);
  or or_12 (MEM_EN, _2, _10, _16);
  or or_13 (LD_MDR, _2, _10, _15);
  or or_14 (GatePC, _1, _13);
  or or_15 (SR2MUX, _6, _8);
  buf or_16 (GateREG, _15);  // OR_Gate
  or or_17 (GateOFFSET, _9, _14);
  or or_18 (GateALU, _4, _5, _6, _7, _8);
  buf or_19 (LD_IR, _3);  // OR_Gate

  // Other names for the same wires on the sheet: ALUKL = ALUK[0]; ALUKM = ALUK[1]; GateOFF = GateOFFSET

  // Notes on the sheet:
  //   eLC-3 CONTROLLER
  //   INPUT SECTION: Do not change anything here!
  //   You may only change the values of the inputs for testing using the hand tool.
  //   Do not introduce a clock or any other input or output pins in the circuit.
  //   NZP
  //   To your logic
  //   OUTPUT SECTION: Do not change anything here!
  //   Do not introduce a clock any other input or output pins in the circuit.
  //   From your logic
endmodule
